// Logisim project LogExemplo_0502.circ as structural Verilog: 1 circuit, main circuit main
module main (
  input  in_1,
  input  in_2,
  output out_3
);

  wire nor_1_out;

  nor nor_1 (nor_1_out, in_1, in_2);
  nor nor_2 (out_3, nor_1_out, nor_1_out);
endmodule
