// Logisim project LogExemplo_0505.circ as structural Verilog: 1 circuit, main circuit main
module main (
  input  in_1,
  input  in_2,
  output out_3
);

  wire nand_1_out, nand_3_out;

  nand nand_1 (nand_1_out, in_1, in_1);
  nand nand_2 (out_3, nand_1_out, nand_3_out);
  nand nand_3 (nand_3_out, in_2, in_2);
endmodule
