// Logisim project LogExemplo_0507.circ as structural Verilog: 1 circuit, main circuit main
module main (
  input  in_1,
  input  in_2,
  output out_3,
  output out_4
);

  wire nand_1_out, nand_2_out, nand_3_out, nand_5_out;

  nand nand_1 (nand_1_out, in_1, in_2);
  nand nand_2 (nand_2_out, in_1, in_1);
  nand nand_3 (nand_3_out, in_2, in_2);
  nand nand_4 (out_3, nand_1_out, nand_5_out);
  nand nand_5 (nand_5_out, nand_2_out, nand_3_out);
  xnor xnor_1 (out_4, in_1, in_2);
endmodule
