// Logisim project Exemplo_0704_Log.circ as structural Verilog: 3 circuits, main circuit main
module main (
  input  in_1,
  input  in_2,
  input  in_3,
  input  in_4,
  input  in_5,
  input  in_6,
  output out_7
);

  wire nor_1_out, or_1_out, xnor_1_out, xor_1_out;

  xor xor_1 (xor_1_out, in_1, in_4);
  xnor xnor_1 (xnor_1_out, in_1, in_4);
  or or_1 (or_1_out, in_5, in_6);
  nor nor_1 (nor_1_out, in_5, in_6);
  Multiplex_4x2 multiplex_4x2_1 (
    .in_3(xor_1_out), .in_4(xnor_1_out), .in_5(or_1_out), .in_6(nor_1_out), .in_1(in_2), .in_2(in_3),
    .out_7(out_7));
endmodule

// 2x1
module Multiplex (
  input  in_1,
  input  in_2,
  input  in_3,
  output out_4
);

  wire and_1_out, and_2_out, not_1_out;

  not not_1 (not_1_out, in_1);
  and and_1 (and_1_out, in_2, not_1_out);
  and and_2 (and_2_out, in_1, in_3);
  or or_1 (out_4, and_1_out, and_2_out);
endmodule

module Multiplex_4x2 (
  input  in_1,
  input  in_2,
  input  in_3,
  input  in_4,
  input  in_5,
  input  in_6,
  output out_7
);

  wire multiplex_1_out_4, multiplex_2_out_4;

  Multiplex multiplex_1 (.in_2(in_3), .in_3(in_4), .in_1(in_1), .out_4(multiplex_1_out_4));
  Multiplex multiplex_2 (.in_2(in_5), .in_3(in_6), .in_1(in_1), .out_4(multiplex_2_out_4));
  Multiplex multiplex_3 (.in_2(multiplex_1_out_4), .in_3(multiplex_2_out_4), .in_1(in_2), .out_4(out_7));
endmodule
