// Logisim project Exemplo_0705_Log.circ as structural Verilog: 2 circuits, main circuit main
module main (
  input  in_1,
  input  in_2,
  input  in_3,
  input  in_4,
  input  in_5,
  input  in_6,
  input  in_7,
  input  in_8,
  input  in_9,
  input  in_10,
  output out_11
);

  wire and_1_out, multiplex_1_out_4, multiplex_2_out_4, multiplex_3_out_4, multiplex_4_out_4,
       multiplex_5_out_4, nand_1_out, nor_1_out, not_1_out, or_1_out, xnor_1_out, xor_1_out;

  not not_1 (not_1_out, in_4);
  or or_1 (or_1_out, in_5, in_6);
  and and_1 (and_1_out, in_7, in_8);
  nor nor_1 (nor_1_out, in_5, in_6);
  nand nand_1 (nand_1_out, in_7, in_8);
  xor xor_1 (xor_1_out, in_9, in_10);
  xnor xnor_1 (xnor_1_out, in_9, in_10);
  Multiplex multiplex_1 (.in_2(not_1_out), .in_3(multiplex_2_out_4), .in_1(in_2), .out_4(multiplex_1_out_4));
  Multiplex multiplex_2 (.in_2(or_1_out), .in_3(nor_1_out), .in_1(in_1), .out_4(multiplex_2_out_4));
  Multiplex multiplex_3 (.in_2(and_1_out), .in_3(nand_1_out), .in_1(in_1), .out_4(multiplex_3_out_4));
  Multiplex multiplex_4 (.in_2(multiplex_3_out_4), .in_3(multiplex_5_out_4), .in_1(in_2), .out_4(multiplex_4_out_4));
  Multiplex multiplex_5 (.in_2(xor_1_out), .in_3(xnor_1_out), .in_1(in_1), .out_4(multiplex_5_out_4));
  Multiplex multiplex_6 (.in_2(multiplex_1_out_4), .in_3(multiplex_4_out_4), .in_1(in_3), .out_4(out_11));
endmodule

// 2x1
module Multiplex (
  input  in_1,
  input  in_2,
  input  in_3,
  output out_4
);

  wire and_1_out, and_2_out, not_1_out;

  not not_1 (not_1_out, in_1);
  and and_1 (and_1_out, in_2, not_1_out);
  and and_2 (and_2_out, in_1, in_3);
  or or_1 (out_4, and_1_out, and_2_out);
endmodule
