// Logisim project Multiplex.circ as structural Verilog: 1 circuit, main circuit Multiplex
module Multiplex (
  input  in_1,
  input  in_2,
  input  in_3,
  output out_4
);

  wire and_1_out, and_2_out, not_1_out;

  not not_1 (not_1_out, in_1);
  and and_1 (and_1_out, in_2, not_1_out);
  and and_2 (and_2_out, in_1, in_3);
  or or_1 (out_4, and_1_out, and_2_out);
endmodule
