// Logisim project Exemplo_0702_Log.circ as structural Verilog: 1 circuit, main circuit main
module main (
  input  in_1,
  input  in_2,
  input  in_3,
  output out_4
);

  wire nor_1_out;

  nor nor_1 (nor_1_out, in_2, in_3);
  xor xor_1 (out_4, in_1, nor_1_out);
endmodule
