// Logisim project Exemplo_0703_Log.circ as structural Verilog: 1 circuit, main circuit main
module main (
  input  in_1,
  input  in_2,
  input  in_3,
  input  in_4,
  input  in_5
);

  wire nand_1_out, nor_1_out, xnor_1_out, xor_1_out;

  xor xor_1 (xor_1_out, in_1, nor_1_out);
  nor nor_1 (nor_1_out, in_2, in_3);
  xnor xnor_1 (xnor_1_out, in_1, nand_1_out);
  nand nand_1 (nand_1_out, in_4, in_5);
endmodule
