// Logisim project Exemplo_0801.circ as structural Verilog: 3 circuits, main circuit Somador
module main (
  input  in_1,
  input  in_2,
  input  in_3,
  input  in_4,
  input  in_5,
  input  in_6,
  input  in_7,
  input  in_8,
  output out_9,
  output out_10,
  output out_11,
  output out_12,
  output out_13
);

  wire somador_1_out_4, somador_3_1_out_5, somador_3_2_out_5;

  Somador somador_1 (.in_1(in_4), .in_2(in_8), .out_3(out_13), .out_4(somador_1_out_4));
  Somador_3 somador_3_1 (.in_1(somador_1_out_4), .in_2(in_3), .in_3(in_7), .out_4(out_12), .out_5(somador_3_1_out_5));
  Somador_3 somador_3_2 (.in_1(somador_3_1_out_5), .in_2(in_2), .in_3(in_6), .out_4(out_11), .out_5(somador_3_2_out_5));
  Somador_3 somador_3_3 (.in_1(somador_3_2_out_5), .in_2(in_1), .in_3(in_5), .out_4(out_10), .out_5(out_9));
endmodule

module Somador (
  input  in_1,
  input  in_2,
  output out_3,
  output out_4
);

  wire not_1_out;

  xor xor_1 (out_3, in_1, in_2);
  not not_1 (not_1_out, out_3);
  and and_1 (out_4, not_1_out, in_2);
endmodule

module Somador_3 (
  input  in_1,
  input  in_2,
  input  in_3,
  output out_4,
  output out_5
);

  wire and_1_out, and_2_out, not_1_out, or_1_out, or_2_out, xor_1_out;

  or or_1 (or_1_out, in_1, in_2);
  and and_1 (and_1_out, in_1, in_2);
  or or_2 (or_2_out, and_1_out, in_3);
  and and_2 (and_2_out, in_3, in_2, in_1);
  not not_1 (not_1_out, xor_1_out);
  xor xor_1 (xor_1_out, or_1_out, or_2_out);
  and and_3 (out_5, or_1_out, not_1_out);
  or or_3 (out_4, xor_1_out, and_2_out);
endmodule
