// Logisim project Somadores.circ as structural Verilog
module Meia_Soma (
  input  X0,
  input  Y0,
  output S0,
  output S1
);

  xor xor_1 (S1, X0, Y0);
  and and_1 (S0, Y0, X0);
endmodule

module Somador_Completo (
  input  Ci0,
  input  X0,
  input  Y0,
  output Co0,
  output S0
);

  wire meia_soma_1_s0, meia_soma_1_s1, meia_soma_2_s0;

  Meia_Soma meia_soma_1 (.X0(X0), .Y0(Y0), .S0(meia_soma_1_s0), .S1(meia_soma_1_s1));
  Meia_Soma meia_soma_2 (.X0(Ci0), .Y0(meia_soma_1_s1), .S0(meia_soma_2_s0), .S1(S0));
  or or_1 (Co0, meia_soma_2_s0, meia_soma_1_s0);
endmodule

module Somador_4_bits (
  input  Ci0,
  input  Y3,
  input  Y2,
  input  Y1,
  input  Y0,
  input  X3,
  input  X2,
  input  X1,
  input  X0,
  output S3,
  output S2,
  output S1,
  output S0,
  output Co0
);

  wire somador_completo_1_co0, somador_completo_2_co0, somador_completo_3_co0;

  Somador_Completo somador_completo_1 (.Ci0(X0), .X0(Y0), .Y0(Ci0), .Co0(somador_completo_1_co0), .S0(S0));
  Somador_Completo somador_completo_2 (
    .Ci0(X1), .X0(Y1), .Y0(somador_completo_1_co0), .Co0(somador_completo_2_co0), .S0(S1));
  Somador_Completo somador_completo_3 (
    .Ci0(X2), .X0(Y2), .Y0(somador_completo_2_co0), .Co0(somador_completo_3_co0), .S0(S2));
  Somador_Completo somador_completo_4 (.Ci0(X3), .X0(Y3), .Y0(somador_completo_3_co0), .Co0(Co0), .S0(S3));
endmodule
