// Logisim project Calculadora Hexadecimal.circ as structural Verilog: 5 circuits, main circuit Somador 4 bits
module Meia_Soma (
  input  X0,
  input  Y0,
  output S0,
  output S1
);

  xor xor_1 (S1, X0, Y0);
  and and_1 (S0, Y0, X0);
endmodule

module Somador_Completo (
  input  Ci0,
  input  X0,
  input  Y0,
  output Co0,
  output S0
);

  wire Meia_Soma_2_s0, Meia_Soma_s0, Meia_Soma_s1;

  Meia_Soma Meia_Soma (.X0(X0), .Y0(Y0), .S0(Meia_Soma_s0), .S1(Meia_Soma_s1));
  Meia_Soma Meia_Soma_2 (.X0(Ci0), .Y0(Meia_Soma_s1), .S0(Meia_Soma_2_s0), .S1(S0));
  or or_1 (Co0, Meia_Soma_2_s0, Meia_Soma_s0);
endmodule

// Somador Completo
module Somador_4_bits (
  input  Ci0,
  input  Y3,
  input  Y2,
  input  Y1,
  input  Y0,
  input  X3,
  input  X2,
  input  X1,
  input  X0,
  output S3,
  output S2,
  output S1,
  output S0,
  output Co0
);

  wire Somador_Completo_2_co0, Somador_Completo_3_co0, Somador_Completo_co0;

  Somador_Completo Somador_Completo (.Ci0(Ci0), .X0(X0), .Y0(Y0), .Co0(Somador_Completo_co0), .S0(S0));
  Somador_Completo Somador_Completo_2 (
    .Ci0(Somador_Completo_co0), .X0(X1), .Y0(Y1), .Co0(Somador_Completo_2_co0), .S0(S1));
  Somador_Completo Somador_Completo_3 (
    .Ci0(Somador_Completo_2_co0), .X0(X2), .Y0(Y2), .Co0(Somador_Completo_3_co0), .S0(S2));
  Somador_Completo Somador_Completo_4 (.Ci0(Somador_Completo_3_co0), .X0(X3), .Y0(Y3), .Co0(Co0), .S0(S3));
endmodule

module Calculadora (
  input  X3,
  input  X2,
  input  X1,
  input  X0,
  input  Ci0,
  input  Y3,
  input  Y2,
  input  Y1,
  input  Y0,
  output S3,
  output S2,
  output S1,
  output S0,
  output Co0
);

  wire decodificador_1_a, decodificador_1_b, decodificador_1_c, decodificador_1_d, decodificador_1_e,
       decodificador_1_f, decodificador_1_g, decodificador_2_a, decodificador_2_b, decodificador_2_c,
       decodificador_2_d, decodificador_2_e, decodificador_2_f, decodificador_2_g, decodificador_3_a,
       decodificador_3_b, decodificador_3_c, decodificador_3_d, decodificador_3_e, decodificador_3_f,
       decodificador_3_g;

  Decodificador decodificador_1 (
    .X3(X3), .X2(X2), .X1(X1), .G(decodificador_1_g), .X0(X0), .F(decodificador_1_f), .A(decodificador_1_a),
    .B(decodificador_1_b), .E(decodificador_1_e), .D(decodificador_1_d), .C(decodificador_1_c));
  Decodificador decodificador_2 (
    .X3(Y3), .X2(Y2), .X1(Y1), .G(decodificador_2_g), .X0(Y0), .F(decodificador_2_f), .A(decodificador_2_a),
    .B(decodificador_2_b), .E(decodificador_2_e), .D(decodificador_2_d), .C(decodificador_2_c));
  _7_Segment_Display u_7_segment_display_1 (
    .g(decodificador_1_g), .f(decodificador_1_f), .a(decodificador_1_a), .b(decodificador_1_b),
    .e(decodificador_1_e), .d(decodificador_1_d), .c(decodificador_1_c));  // open: dp
  Somador_4_bits somador_4_bits_1 (
    .Y3(Y3), .Y2(Y2), .Y1(Y1), .Y0(Y0), .X3(X3), .X2(X2), .X1(X1), .X0(X0), .Ci0(Ci0), .S3(S3), .S2(S2),
    .S1(S1), .S0(S0), .Co0(Co0));
  _7_Segment_Display u_7_segment_display_2 (
    .g(decodificador_2_g), .f(decodificador_2_f), .a(decodificador_2_a), .b(decodificador_2_b),
    .e(decodificador_2_e), .d(decodificador_2_d), .c(decodificador_2_c));  // open: dp
  Decodificador decodificador_3 (
    .X3(S3), .X2(S2), .X1(S1), .G(decodificador_3_g), .X0(S0), .F(decodificador_3_f), .A(decodificador_3_a),
    .B(decodificador_3_b), .E(decodificador_3_e), .D(decodificador_3_d), .C(decodificador_3_c));
  _7_Segment_Display u_7_segment_display_3 (
    .g(decodificador_3_g), .f(decodificador_3_f), .a(decodificador_3_a), .b(decodificador_3_b),
    .e(decodificador_3_e), .d(decodificador_3_d), .c(decodificador_3_c));  // open: dp
endmodule

module Decodificador (
  input  X3,
  input  X2,
  input  X1,
  input  X0,
  output G,
  output F,
  output A,
  output B,
  output E,
  output D,
  output C
);

  wire and_1_out, and_2_out, and_3_out, and_4_out, and_5_out, and_6_out, and_7_out, and_8_out, and_9_out,
       and_10_out, and_11_out, and_12_out, and_13_out, and_14_out, and_15_out, and_16_out, and_17_out,
       and_18_out, and_19_out, and_20_out, and_21_out, and_22_out, and_23_out, and_24_out, and_25_out,
       and_26_out, and_27_out, and_28_out, and_29_out, and_30_out, and_31_out, and_32_out, and_33_out,
       and_34_out, and_35_out, not_1_out, not_2_out, not_3_out, not_4_out, not_5_out, not_6_out, not_7_out,
       not_8_out, not_9_out, not_10_out, not_11_out, not_12_out, not_13_out, not_14_out, not_15_out,
       not_16_out, not_17_out, not_18_out, not_19_out, not_20_out, not_21_out, not_22_out, not_23_out,
       not_24_out, not_25_out, not_26_out, not_27_out, not_28_out, not_29_out, not_30_out, not_31_out,
       not_32_out, not_33_out, not_34_out, not_35_out, not_36_out, not_37_out, not_38_out, not_39_out,
       not_40_out, not_41_out, not_42_out, not_43_out, not_44_out;

  not not_1 (not_1_out, X2);
  and and_1 (and_1_out, not_1_out, X1);
  and and_2 (and_2_out, X1, not_2_out);
  not not_2 (not_2_out, X0);
  not not_3 (not_3_out, X3);
  and and_3 (and_3_out, not_3_out, X2, not_4_out);
  not not_4 (not_4_out, X1);
  and and_4 (and_4_out, X3, not_5_out);
  not not_5 (not_5_out, X2);
  and and_5 (and_5_out, X3, X0);
  not not_6 (not_6_out, X1);
  and and_6 (and_6_out, not_6_out, not_7_out);
  not not_7 (not_7_out, X0);
  not not_8 (not_8_out, X3);
  and and_7 (and_7_out, not_8_out, X2, not_9_out);
  not not_9 (not_9_out, X1);
  and and_8 (and_8_out, X2, not_10_out);
  not not_10 (not_10_out, X0);
  and and_9 (and_9_out, X3, not_11_out);
  not not_11 (not_11_out, X2);
  and and_10 (and_10_out, X3, X1);
  not not_12 (not_12_out, X2);
  and and_11 (and_11_out, not_12_out, not_13_out);
  not not_13 (not_13_out, X0);
  not not_14 (not_14_out, X3);
  and and_12 (and_12_out, not_14_out, X1);
  not not_15 (not_15_out, X3);
  and and_13 (and_13_out, not_15_out, X2, X0);
  and and_14 (and_14_out, X2, X1);
  and and_15 (and_15_out, X3, not_16_out, not_17_out);
  not not_16 (not_16_out, X2);
  not not_17 (not_17_out, X1);
  and and_16 (and_16_out, X3, not_18_out);
  not not_18 (not_18_out, X0);
  not not_19 (not_19_out, X3);
  and and_17 (and_17_out, not_19_out, not_20_out);
  not not_20 (not_20_out, X2);
  not not_21 (not_21_out, X3);
  not not_22 (not_22_out, X1);
  and and_18 (and_18_out, not_21_out, not_22_out, not_23_out);
  not not_23 (not_23_out, X0);
  not not_24 (not_24_out, X2);
  and and_19 (and_19_out, not_24_out, not_25_out);
  not not_25 (not_25_out, X0);
  not not_26 (not_26_out, X3);
  and and_20 (and_20_out, not_26_out, X1, X0);
  not not_27 (not_27_out, X1);
  and and_21 (and_21_out, X3, not_27_out, X0);
  not not_28 (not_28_out, X2);
  and and_22 (and_22_out, not_28_out, not_29_out);
  not not_29 (not_29_out, X0);
  and and_23 (and_23_out, X1, not_30_out);
  not not_30 (not_30_out, X0);
  and and_24 (and_24_out, X3, X1);
  and and_25 (and_25_out, X3, X2);
  not not_31 (not_31_out, X3);
  not not_32 (not_32_out, X2);
  and and_26 (and_26_out, not_31_out, not_32_out, not_33_out);
  not not_33 (not_33_out, X0);
  not not_34 (not_34_out, X2);
  and and_27 (and_27_out, not_34_out, X1, X0);
  not not_35 (not_35_out, X1);
  and and_28 (and_28_out, X2, not_35_out, X0);
  and and_29 (and_29_out, X2, X1, not_36_out);
  not not_36 (not_36_out, X0);
  and and_30 (and_30_out, X3, not_37_out, not_38_out);
  not not_37 (not_37_out, X1);
  not not_38 (not_38_out, X0);
  not not_39 (not_39_out, X3);
  and and_31 (and_31_out, not_39_out, not_40_out);
  not not_40 (not_40_out, X1);
  not not_41 (not_41_out, X3);
  and and_32 (and_32_out, not_41_out, X0);
  not not_42 (not_42_out, X1);
  and and_33 (and_33_out, not_42_out, X0);
  not not_43 (not_43_out, X3);
  and and_34 (and_34_out, not_43_out, X2);
  and and_35 (and_35_out, X3, not_44_out);
  not not_44 (not_44_out, X2);
  or or_1 (G, and_1_out, and_2_out, and_3_out, and_4_out, and_5_out);
  or or_2 (F, and_6_out, and_7_out, and_8_out, and_9_out, and_10_out);
  or or_3 (B, and_17_out, and_18_out, and_19_out, and_20_out, and_21_out);
  or or_4 (E, and_22_out, and_23_out, and_24_out, and_25_out);
  or or_5 (D, and_26_out, and_27_out, and_28_out, and_29_out, and_30_out);
  or or_6 (C, and_31_out, and_32_out, and_33_out, and_34_out, and_35_out);
  or or_7 (A, and_11_out, and_12_out, and_13_out, and_14_out, and_15_out, and_16_out);
endmodule
