// Logisim project ULA.circ as structural Verilog: 6 circuits, main circuit ULA 4 bits
// MUX
module MUX_4_bits (
  input  X,
  input  Y,
  input  Z,
  input  K,
  input  OP1,
  input  OP0,
  output OUT
);

  wire and_1_out, and_2_out, and_3_out, and_4_out;

  and and_1 (and_1_out, X, ~OP0, ~OP1);  // AND_Gate
  and and_2 (and_2_out, Y, OP0, ~OP1);  // AND_Gate
  and and_3 (and_3_out, Z, ~OP0, OP1);  // AND_Gate
  and and_4 (and_4_out, K, OP0, OP1);
  or or_1 (OUT, and_1_out, and_2_out, and_3_out, and_4_out);
endmodule

module MUX_2_bits (
  input  A,
  input  B,
  input  OP0,
  output OUT
);

  wire and_1_out, and_2_out;

  and and_1 (and_1_out, A, ~OP0);  // AND_Gate
  and and_2 (and_2_out, B, OP0);
  or or_1 (OUT, and_1_out, and_2_out);
endmodule

module Somador_Completo (
  input  Ci0,
  input  X0,
  input  Y0,
  output S0,
  output Co0
);

  wire Meia_Soma_2_s0, Meia_Soma_s0, Meia_Soma_s1;

  Meio_Somador Meia_Soma (.X0(X0), .Y0(Y0), .S0(Meia_Soma_s0), .S1(Meia_Soma_s1));
  Meio_Somador Meia_Soma_2 (.X0(Ci0), .Y0(Meia_Soma_s1), .S0(Meia_Soma_2_s0), .S1(S0));
  or or_1 (Co0, Meia_Soma_2_s0, Meia_Soma_s0);
endmodule

module Meio_Somador (
  input  X0,
  input  Y0,
  output S0,
  output S1
);

  xor xor_1 (S1, X0, Y0);
  and and_1 (S0, Y0, X0);
endmodule

// ULA 2b
module ULA_2_bits (
  input  Ci0,
  input  A,
  input  B,
  input  Bivolt,
  input  OP1,
  input  OP0,
  output OUT,
  output Co0
);

  wire and_1_out, mux_2_bits_1_out, not_1_out, not_2_out, or_1_out, Somador_s0;

  MUX_2_bits mux_2_bits_1 (.A(B), .B(not_1_out), .OP0(Bivolt), .OUT(mux_2_bits_1_out));
  not not_1 (not_1_out, B);
  and and_1 (and_1_out, A, B);
  or or_1 (or_1_out, A, B);
  not not_2 (not_2_out, A);
  Somador_Completo Somador (.X0(A), .Y0(mux_2_bits_1_out), .Ci0(Ci0), .S0(Somador_s0), .Co0(Co0));
  MUX_4_bits mux_4_bits_1 (.X(and_1_out), .Y(or_1_out), .Z(not_2_out), .K(Somador_s0), .OP1(OP1), .OP0(OP0), .OUT(OUT));
endmodule

module ULA_4_bits (
  input  A0,
  input  B0,
  input  A1,
  input  B1,
  input  Bivolt,
  input  OP1,
  input  OP0,
  output Out_0,
  output Out_1,
  output Co0
);

  wire ula_2_bits_1_co0;

  ULA_2_bits ula_2_bits_1 (
    .A(A0), .B(B0), .Ci0(Bivolt), .Bivolt(Bivolt), .Co0(ula_2_bits_1_co0), .OP1(OP1), .OP0(OP0), .OUT(Out_0));
  ULA_2_bits ula_2_bits_2 (
    .A(A1), .B(B1), .Ci0(ula_2_bits_1_co0), .Bivolt(Bivolt), .Co0(Co0), .OP1(OP1), .OP0(OP0), .OUT(Out_1));

  // Notes on the sheet:
  //   Ci0
endmodule
