// Logisim project Multiplicador.circ as structural Verilog: 4 circuits, main circuit Meio Somador
module \Multiplicação  (
  input  A1,
  input  A2,
  input  A4,
  input  A8,
  input  B1,
  input  B2,
  input  B4,
  input  B8,
  output P1,
  output P2,
  output P4,
  output P8,
  output P16,
  output P32,
  output P64,
  output P128
);

  Multiplicador_8_bits Multiplicador (
    .A1(A1), .B1(B1), .A2(A2), .B2(B2), .A4(A4), .B4(B4), .A8(A8), .B8(B8), .P1(P1), .P2(P2), .P4(P4),
    .P8(P8), .P16(P16), .P32(P32), .P64(P64), .P128(P128));
endmodule

module Meio_Somador (
  input  A0,
  input  B0,
  output S1,
  output S0
);

  xor xor_1 (S0, A0, B0);
  and and_1 (S1, B0, A0);
endmodule

// Soma
module Somador_Completo (
  input  Ci0,
  input  A0,
  input  B0,
  output Co0,
  output S0
);

  wire meio_somador_1_s0, meio_somador_1_s1, meio_somador_2_s1;

  Meio_Somador meio_somador_1 (.A0(A0), .B0(B0), .S1(meio_somador_1_s1), .S0(meio_somador_1_s0));
  Meio_Somador meio_somador_2 (.A0(Ci0), .B0(meio_somador_1_s0), .S1(meio_somador_2_s1), .S0(S0));
  or or_1 (Co0, meio_somador_2_s1, meio_somador_1_s1);
endmodule

module Multiplicador_8_bits (
  input  A1,
  input  B1,
  input  A2,
  input  B2,
  input  A4,
  input  B4,
  input  A8,
  input  B8,
  output P1,
  output P2,
  output P4,
  output P8,
  output P16,
  output P32,
  output P64,
  output P128
);

  wire A1B2_out, A1B4_2_out, A1B4_out, A2B1_out, A2B2_out, A2B4_out, A2B8_out, A4B1_out, A4B2_out, A4B4_out,
       A4B8_out, A8B1_out, A8B2_out, A8B4_out, A8B8_out, somador_completo_1_co0, somador_completo_2_co0,
       somador_completo_2_s0, somador_completo_3_co0, somador_completo_3_s0, somador_completo_4_co0,
       somador_completo_5_co0, somador_completo_5_s0, somador_completo_6_co0, somador_completo_6_s0,
       somador_completo_7_co0, somador_completo_7_s0, somador_completo_8_co0, somador_completo_8_s0,
       somador_completo_9_co0, somador_completo_9_s0, somador_completo_10_co0, somador_completo_11_co0,
       somador_completo_11_s0, somador_completo_12_co0, somador_completo_13_co0, somador_completo_13_s0,
       somador_completo_14_co0, somador_completo_14_s0, somador_completo_15_co0, somador_completo_16_co0;

  and A1B1 (P1, A1, B1);
  and A2B1 (A2B1_out, B1, A2);
  Somador_Completo somador_completo_1 (.Ci0(1'b0), .A0(A2B1_out), .B0(A1B2_out), .Co0(somador_completo_1_co0), .S0(P2));
  and A1B2 (A1B2_out, A1, B2);
  and A1B4 (A1B4_out, A1, B4);
  Somador_Completo somador_completo_2 (
    .Ci0(somador_completo_1_co0), .A0(1'b0), .B0(A1B4_out), .Co0(somador_completo_2_co0),
    .S0(somador_completo_2_s0));
  and A2B2 (A2B2_out, A2, B2);
  Somador_Completo somador_completo_3 (
    .Ci0(1'b0), .A0(A2B2_out), .B0(A4B1_out), .Co0(somador_completo_3_co0), .S0(somador_completo_3_s0));
  and A4B1 (A4B1_out, A4, B1);
  and A1B4_2 (A1B4_2_out, A1, B4);
  and A2B4 (A2B4_out, A2, B4);
  and A4B2 (A4B2_out, A4, B2);
  and A8B1 (A8B1_out, A8, B1);
  and A2B8 (A2B8_out, A2, B8);
  and A4B4 (A4B4_out, A4, B4);
  and A8B2 (A8B2_out, A8, B2);
  and A4B8 (A4B8_out, A4, B8);
  and A8B4 (A8B4_out, A8, B4);
  and A8B8 (A8B8_out, A8, B8);
  Somador_Completo somador_completo_4 (
    .Ci0(somador_completo_2_s0), .A0(somador_completo_3_s0), .B0(somador_completo_5_s0),
    .Co0(somador_completo_4_co0), .S0(P4));
  Somador_Completo somador_completo_5 (
    .Ci0(1'b0), .A0(somador_completo_3_co0), .B0(somador_completo_2_co0), .Co0(somador_completo_5_co0),
    .S0(somador_completo_5_s0));
  Somador_Completo somador_completo_6 (
    .Ci0(somador_completo_4_co0), .A0(A1B4_2_out), .B0(A2B4_out), .Co0(somador_completo_6_co0),
    .S0(somador_completo_6_s0));
  Somador_Completo somador_completo_7 (
    .Ci0(1'b0), .A0(A4B2_out), .B0(A8B1_out), .Co0(somador_completo_7_co0), .S0(somador_completo_7_s0));
  Somador_Completo somador_completo_8 (
    .Ci0(1'b0), .A0(somador_completo_7_co0), .B0(somador_completo_6_co0), .Co0(somador_completo_8_co0),
    .S0(somador_completo_8_s0));
  Somador_Completo somador_completo_9 (
    .Ci0(1'b0), .A0(somador_completo_5_co0), .B0(A8B2_out), .Co0(somador_completo_9_co0),
    .S0(somador_completo_9_s0));
  Somador_Completo somador_completo_10 (
    .Ci0(somador_completo_6_s0), .A0(somador_completo_7_s0), .B0(somador_completo_8_s0),
    .Co0(somador_completo_10_co0), .S0(P8));
  Somador_Completo somador_completo_11 (
    .Ci0(somador_completo_10_co0), .A0(A2B8_out), .B0(A4B4_out), .Co0(somador_completo_11_co0),
    .S0(somador_completo_11_s0));
  Somador_Completo somador_completo_12 (
    .Ci0(somador_completo_11_s0), .A0(somador_completo_9_s0), .B0(somador_completo_13_s0),
    .Co0(somador_completo_12_co0), .S0(P16));
  Somador_Completo somador_completo_13 (
    .Ci0(somador_completo_11_co0), .A0(somador_completo_9_co0), .B0(1'b0), .Co0(somador_completo_13_co0),
    .S0(somador_completo_13_s0));
  Somador_Completo somador_completo_14 (
    .Ci0(somador_completo_12_co0), .A0(A4B8_out), .B0(A8B4_out), .Co0(somador_completo_14_co0),
    .S0(somador_completo_14_s0));
  Somador_Completo somador_completo_15 (
    .Ci0(somador_completo_14_co0), .A0(somador_completo_13_co0), .B0(A8B8_out),
    .Co0(somador_completo_15_co0), .S0(P64));
  Somador_Completo somador_completo_16 (
    .Ci0(somador_completo_14_s0), .A0(1'b0), .B0(somador_completo_8_co0), .Co0(somador_completo_16_co0),
    .S0(P32));
  Somador_Completo somador_completo_17 (
    .Ci0(somador_completo_16_co0), .A0(somador_completo_15_co0), .B0(1'b0), .S0(P128));  // open: Co0
endmodule
